# Fritzing sketch v20 (saved by Fritzing 0.9.3b)
perfboards: 1

parts:
  U3 = NodeMCU V1.0
  Part2 = Bluetooth HM-10
  J5 = female pin header, 3 pins [form="♀ (female)"]  # not connected
  J6 = female pin header, 4 pins [form="♀ (female)"]
  J7 = female pin header, 3 pins [form="♀ (female)"]
  J8 = female pin header, 4 pins [form="♀ (female)"]  # not connected
  LED3 = smd LED [color="Blue (430nm)" package="1206 [SMD]"]
  LED4 = smd LED [color="Red (633nm)" package="1206 [SMD]"]
  R3 = Resistor [tolerance=±5% resistance=220 package=THT]
  R4 = Resistor [tolerance=±5% resistance=220 package=THT]
  DHT2 = DHT11 Humitidy and Temperature Sensor
  PIR2 = PIR sensor

nets:
  N1: U3.D1, J7.pin2, PIR2.SIG
  N2: U3.D2, R3.Pin_0
  N3: U3.D3, R4.Pin_0
  N4: U3.D4, DHT2.DATA
  3V3: U3.3V3, DHT2.VDD
  GND: U3.GND, J7.pin1, DHT2.GND, PIR2.GND
  N5: U3.RX, Part2.TXD
  N6: U3.TX, Part2.RXD
  VIN: U3.Vin, J7.pin3, PIR2.VDD
  N7: Part2.GND, J6.pin2
  N8: Part2.VCC, J6.pin1
  N9: LED3.cathode, LED4.cathode
  N10: LED3.anode, R3.Pin_1
  N11: LED4.anode, R4.Pin_1

notes:
  MQ-2 sensor board,
  with connected
  VCC, GND and Analog input

custom parts:
  NodeMCU V1.0: ESP8266 based NodeMCU
  DHT11 Humitidy and Temperature Sensor: DHT11 Humidity and Temperature Sensor
